# Fritzing sketch Snake-ino (saved by Fritzing 0.9.4)
breadboards: 1

parts:
  8x8_LED_Modul_mit_MAX1 = 8x8 LED Modul mit MAX7219 [package=THT]
  Analog_Joystick = Thumb Joystick
  Arduino = Arduino Uno (Rev3)

nets:
  VCC: 8x8_LED_Modul_mit_MAX1.VCC_Eingang, Analog_Joystick.VCC, Arduino.5V
  GND: 8x8_LED_Modul_mit_MAX1.GND_Eingang, Analog_Joystick.GND, Arduino.GND
  N1: 8x8_LED_Modul_mit_MAX1.DIN_Eingang, Arduino.D8
  N2: 8x8_LED_Modul_mit_MAX1.CS_Eingang, Arduino.D9_PWM
  N3: 8x8_LED_Modul_mit_MAX1.CLK_Eingang, Arduino.D10_PWM/SS
  N4: Analog_Joystick.SEL, Arduino.D2
  N5: Analog_Joystick.HORZ, Arduino.A4/SDA
  N6: Analog_Joystick.VERT, Arduino.A3
